# Fritzing sketch Schematics (saved by Fritzing 0.9.10b)
breadboards: 1

parts:
  LCM1602_IIC1 = LCM1602 IIC [part_number="LCM1602 IIC" chip_label="LCM1602 IIC" package="DIP (Dual Inline) [THT]"]
  U1 = LCD-16X2 [package=lcd-16x2_noholes]
  Part1 = Arduino Uno (Rev3) - ICSP
  J1 = Piezo Speaker
  S1 = Pushbutton [package="[THT]"]
  S2 = Pushbutton [package="[THT]"]
  S3 = Pushbutton [package="[THT]"]
  R1 = Resistor [tolerance=±5% resistance=10000 package="0603 [SMD]"]
  R2 = Resistor [tolerance=±5% resistance=10000 package="2512 [SMD]"]
  R3 = Resistor [tolerance=±5% resistance=10000 package="2010 [SMD]"]

nets:
  VSS: LCM1602_IIC1.VSS, U1.VSS
  VDD: LCM1602_IIC1.VDD, U1.VDD
  N1: LCM1602_IIC1.V0, U1.VO
  N2: LCM1602_IIC1.RS, U1.RS
  N3: LCM1602_IIC1.RW, U1.R_W
  N4: LCM1602_IIC1.E, U1.E
  N5: LCM1602_IIC1.D0, U1.DB0
  N6: LCM1602_IIC1.D1, U1.DB1
  N7: LCM1602_IIC1.D2, U1.DB2
  N8: LCM1602_IIC1.D3, U1.DB3
  N9: LCM1602_IIC1.D4, U1.DB4
  N10: LCM1602_IIC1.D5, U1.DB5
  N11: LCM1602_IIC1.D6, U1.DB6
  N12: LCM1602_IIC1.D7, U1.DB7
  N13: LCM1602_IIC1.A, U1.A
  N14: LCM1602_IIC1.K, U1.K
  GND: LCM1602_IIC1.GND, Part1.GND, J1.pin1, S1.Pin_1, S1.Pin_2, S2.Pin_1, S2.Pin_2, S3.Pin_1, S3.Pin_2
  VCC: LCM1602_IIC1.VCC, Part1.5V, R1.Pin_1, R2.Pin_1, R3.Pin_1
  N15: LCM1602_IIC1.SDA, Part1.A4/SDA
  N16: LCM1602_IIC1.SCL, Part1.A5/SCL
  N17: Part1.D10_PWM/SS, S1.Pin_3, S1.Pin_4, R1.Pin_0
  N18: Part1.D11_PWM/MOSI, S3.Pin_3, S3.Pin_4, R3.Pin_0
  N19: Part1.D12/MISO, S2.Pin_3, S2.Pin_4, R2.Pin_0
  N20: Part1.D13/SCK, J1.pin2

custom parts:
  LCM1602 IIC: I2C-Module to use a 1602 or 2004 LCD on with the wire.h libory Serial LCD Modul
